# Fritzing sketch Schematic (saved by Fritzing 0.9.4)
breadboards: 1

parts:
  Componente1 = Arduino Uno (Rev3)
  Componente2 = Arduino Nano (Rev3.0)
  M1 = Niren can bus module [package=THT]
  M2 = Niren can bus module [package=THT]

nets:
  N1: Componente1.D10_PWM/SS, M1.pin3
  N2: Componente1.D11_PWM/MOSI, M1.pin5
  N3: Componente1.D12/MISO, M1.pin4
  N4: Componente1.D13/SCK, M1.pin6
  N5: Componente1.5V, M1.pin1
  N6: Componente1.GND, M1.pin2
  N7: Componente2.GND, M2.pin2
  N8: Componente2.D10, M2.pin3
  N9: Componente2.D11/MOSI, M2.pin6
  N10: Componente2.D12/MISO, M2.pin4
  N11: Componente2.5V, M2.pin1
  N12: Componente2.D13/SCK, M2.pin5
  N13: M1.pin12, M2.pin10, M2.pin12
  N14: M1.pin13, M2.pin11, M2.pin13

custom parts:
  Niren can bus module: Niren can bus module availabe on ebay and others. Pcb view assumes that you unsolder the 7 pin header and resolder it on the bottom of the module to connect to the pcb. The two jumpers and the can bus connector remain on the top of the board and don't appear in pcb view.
